# Fritzing sketch multiplexer wiring diagram (saved by Fritzing 0.9.8b)

parts:
  Part1 = Analog Digital MUX Breakout
  Part2 = Arduino Mega ADK (Rev3)
  S1 = Round Pushbutton
  S2 = Round Pushbutton
  S3 = Taiway 100-SP-X-T1 SPDT Miniature Toggle Switch [part_number=100-SP-X-T1-0-0-B1-M2 package=THT]

nets:
  N1: Part1.C0, S2.leg1
  N2: Part1.C1, S3.COM
  N3: Part1.C5, S1.leg1
  GND: Part1.GND, Part2.GND
  VCC: Part1.VCC, Part2.5V
  N4: Part1.S0, Part2.D3_PWM
  N5: Part1.S1, Part2.D4_PWM
  N6: Part1.S2, Part2.D5_PWM
  N7: Part1.S3, Part2.D6_PWM
  N8: Part1.SIG, Part2.D7_PWM
