# Fritzing sketch Circuit Layout (saved by Fritzing 0.9.8b)

parts:
  RE1 = KY-040 Rotary encoder [package=THT]
  Part1 = Arduino Mega 2560 (Rev3)
  S1 = Round Pushbutton
  S2 = Round Pushbutton
  LCD2004-I2C1 = LCD2004-I2C

nets:
  GND: RE1.GND, Part1.GND
  N1: RE1.SW, Part1.D16_PWM/TX2
  N2: RE1.DT, Part1.D18/TX1
  N3: RE1.CLK, Part1.D19/RX1
  N4: Part1.D21/SCL, LCD2004-I2C1.SCL
  N5: Part1.D20/SDA, LCD2004-I2C1.SDA
  N6: Part1.D9_PWM, S1.leg1
  5V: Part1.5V, LCD2004-I2C1.VCC
  N7: Part1.D7_PWM, S2.leg1

custom parts:
  KY-040 Rotary encoder: KY-040 Rotary Encoder with switch on breakout borad from AZ Delivery
  LCD2004-I2C: A standard character display with 4x20 characters. Comes in many colors with LCM2004 IIC attached.
