# Fritzing sketch Circuit Layout (saved by Fritzing 0.9.8b)

parts:
  Part2 = Arduino Mega 2560 (Rev3)
  S1 = Taiway 100-SP-X-T1 SPDT Miniature Toggle Switch [part_number=100-SP-X-T1-0-0-B1-M1 package=THT]
  S2 = Taiway 100-SP-X-T1 SPDT Miniature Toggle Switch [part_number=100-SP-X-T1-0-0-B1-M1 package=THT]
  S3 = Square Pushbutton
  S4 = Square Pushbutton
  S5 = Square Pushbutton

nets:
  N1: Part2.D45, S3.leg0
  N2: Part2.D47, S2.L2
  N3: Part2.D49, S4.leg0
  N4: Part2.D51, S5.leg1
  N5: Part2.D53, S1.L2
  N6: Part2.GND, S1.L1, S2.L1
  N7: S3.leg1, S5.leg0
